# Fritzing sketch WifiLedPrototypefzz (saved by Fritzing 0.9.3b)
breadboards: 1

parts:
  U1 = NodeMCU V1.0
  LED1 = smd LED [color="Red (633nm)" package="0805 [SMD]"]
  LED2 = smd LED [color="Green (555nm)" package="0805 [SMD]"]
  LED3 = smd LED [color="Yellow (595nm)" package="0805 [SMD]"]
  R1 = Resistor [tolerance=±5% resistance=300 package="1206 [SMD]"]
  R2 = Resistor [tolerance=±5% resistance=300 package="1206 [SMD]"]
  R3 = Resistor [tolerance=±5% resistance=300 package="1206 [SMD]"]

nets:
  N1: U1.D1, LED1.anode
  N2: U1.D2, LED2.anode
  N3: U1.D3, LED3.anode
  N4: U1.GND, R1.Pin_0, R2.Pin_0, R3.Pin_0
  N5: LED1.cathode, R1.Pin_1
  N6: LED2.cathode, R2.Pin_1
  N7: LED3.cathode, R3.Pin_1

custom parts:
  NodeMCU V1.0: ESP8266 based NodeMCU
